# Fritzing sketch CLOCK (saved by Fritzing 0.8.7b)
circuit board: 8.46667cm x 5.64444cm
breadboards: 1

parts:
  Arduino = Arduino Nano (Rev3.0)
  MAX1 = Max7219 [chip_label=Max7219 package="DIP (Dual Inline) [THT]"]
  part = LED Dot Matrix 18mm (0.7 INCH)
  LEDs = LED Dot Matrix 18mm (0.7 INCH)
  hours_button = SWITCH-MOMENTARY-2 [package=tactile_switch_smd-2]
  minutes_button = SWITCH-MOMENTARY-2 [package=tactile_switch_smd-2]
  R1 = Resistor [tolerance=±5% resistance=10k package="0805 [SMD]"]
  R2 = Resistor [tolerance=±5% resistance=10k package="0805 [SMD]"]
  RTC = DS1307 [package=so08]

nets:
  GND: Arduino.GND, R1.Pin_1, R2.Pin_1, RTC.GND
  N1: Arduino.D2, MAX1.Din
  N2: Arduino.D3, MAX1.Load(CS)
  N3: Arduino.D5, MAX1.Clk
  N4: Arduino.D11/MOSI, minutes_button.2, R1.Pin_0
  N5: Arduino.D12/MISO, hours_button.2, R2.Pin_0
  5V: Arduino.5V, MAX1.V++, hours_button.1, minutes_button.1, RTC.VCC
  N6: MAX1.Dig0, part.Column_1
  N7: MAX1.Dig4, LEDs.Column_4
  N8: MAX1.Dig2, LEDs.Column_2
  N9: MAX1.Dig3, LEDs.Column_3
  N10: MAX1.Dig5, LEDs.Column_5
  N11: MAX1.Dig1, LEDs.Column_1
  N12: MAX1.SegA, part.Row_1
  N13: MAX1.SegF, part.Row_6
  N14: MAX1.SegB, part.Row_2
  N15: MAX1.SegG, part.Row_7
  N16: MAX1.SegC, part.Row_3
  N17: MAX1.SegE, part.Row_5
  N18: MAX1.SegD, part.Row_4

custom parts:
  Max7219: Labled part for Maxim MAX7219 LED driver. With 24 pins on a 300mil dual inline package (DIP) footprint.
